# Fritzing sketch a-bot (saved by Fritzing 0.9.3b)
circuit board: 7.39658cm x 3.69475cm
breadboards: 1

parts:
  M1 = DC Motor
  M2 = DC Motor
  L293 = L293D [package=THT]
  BAT = male pin header, 3 pins [form="♂ (male)"]
  E1 = male pin header, 3 pins [form="♂ (male)"]
  E2 = male pin header, 3 pins [form="♂ (male)"]
  KP = male pin header, 3 pins [form="♂ (male)"]
  Photon = Photon

nets:
  N1: M1.pin_1, L293.Out_2_(_Controlled_by_Enable_1_)
  N2: M1.pin_2, L293.Out_1_(_Controlled_by_Enable_1_)
  N3: M2.pin_1, L293.Out_4_(_Controlled_by_Enable_2_)
  N4: M2.pin_2, L293.Out_3_(_Controlled_by_Enable_2_)
  N5: L293.Enable_1, Photon.A4
  N6: L293.In_1, Photon.A1
  N7: L293.0V, BAT.pin1, E1.pin1, E2.pin1, KP.pin1, Photon.GND
  N8: L293.In_2, Photon.A0
  N9: L293.+Vmotor, L293.+V, BAT.pin2, E1.pin2, E2.pin2, Photon.VIN
  N10: L293.Enable_2, Photon.D0
  N11: L293.In_3, Photon.D2
  N12: L293.In_4, Photon.D1
  N13: E1.pin3, Photon.D3
  N14: E2.pin3, Photon.D5
  N15: KP.pin2, Photon.3V3
  N16: KP.pin3, Photon.A5
